# Fritzing sketch IMU_Servo_Wire (saved by Fritzing 0.9.3b)
breadboards: 1

parts:
  Part1 = Arduino Mega 2560 (Rev3)
  J1 = Basic Servo
  J2 = Basic Servo
  Part2 = InvenSense MPU6050

nets:
  N1: Part1.SCL, Part2.SCL
  N2: Part1.SDA, Part2.SDA
  VCC: Part1.5V, J1.vcc, J2.vcc, Part2.VCC
  GND: Part1.GND, J1.gnd, J2.gnd, Part2.GND
  N3: Part1.D2_PWM, Part2.INT
  N4: Part1.D3_PWM, J1.pulse
  N5: Part1.D4_PWM, J2.pulse
